// Logisim project sumador_simple.circ as structural Verilog: 1 circuit, main circuit main
module main (
  input  in_1,
  input  in_2,
  output res,
  output carry
);

  xor xor_1 (res, in_1, in_2);
  and and_1 (carry, in_1, in_2);

  // Notes on the sheet:
  //   Sumador Simple
endmodule
