// Logisim project ej5.circ as structural Verilog: 1 circuit, main circuit main
module main (
  input  Ejercicio_5,
  input  in_2,
  input  in_3,
  output out_4
);

  wire nor_1_out, not_1_out, not_2_out, not_3_out, not_4_out;

  not not_1 (not_1_out, Ejercicio_5);
  not not_2 (not_2_out, in_2);
  not not_3 (not_3_out, in_3);
  nor nor_1 (nor_1_out, not_1_out, not_2_out);
  not not_4 (not_4_out, nor_1_out);
  nor nor_2 (out_4, not_4_out, not_3_out);
endmodule
