// Logisim project ej8b.circ as structural Verilog: 1 circuit, main circuit main
module main (
  input  e1,
  input  e2,
  input  e3,
  input  e4,
  output out
);

  wire and_1_out, and_2_out, and_3_out, and_4_out, not_1_out, not_2_out, not_3_out, not_4_out, xor_1_out,
       xor_2_out;

  not not_1 (not_1_out, e3);
  not not_2 (not_2_out, e4);
  not not_3 (not_3_out, e1);
  not not_4 (not_4_out, e2);
  xor xor_1 (xor_1_out, e1, e2);
  and and_1 (and_1_out, not_1_out, not_2_out);
  and and_2 (and_2_out, not_3_out, not_4_out);
  xor xor_2 (xor_2_out, e4, e3);
  and and_3 (and_3_out, xor_1_out, and_1_out);
  and and_4 (and_4_out, and_2_out, xor_2_out);
  or or_1 (out, and_3_out, and_4_out);

  // Notes on the sheet:
  //   Ejercicio 8 - Input valido
  //   f(e1, e2, e3, e4) = 1 <=> exists ! i | 1 <= i <= 4 && e_i in [0,1] && 
  //   forall j | 1 <= j <= 4 && j != i --> e_j = 0
endmodule
